// Logisim project 4X16_Decoder_Assgn_3.circ as structural Verilog: 1 circuit, main circuit main
module main (
  input  A,
  input  B,
  input  C,
  input  D,
  output [15:0] out_5
);

  wire not_1_out, not_3_out, not_4_out;

  not not_1 (not_1_out, A);
  not not_2 (not_1_out, B);
  not not_3 (not_3_out, D);
  not not_4 (not_4_out, C);
  and and_1 (out_5[0], not_1_out, not_1_out, not_4_out, not_3_out);
  and and_2 (out_5[1], not_1_out, not_1_out, not_4_out, D);
  and and_3 (out_5[2], not_1_out, not_1_out, C, not_3_out);
  and and_4 (out_5[3], not_1_out, not_1_out, C, D);
  and and_5 (out_5[4], not_1_out, B, not_4_out, not_3_out);
  and and_6 (out_5[5], not_1_out, B, not_4_out, D);
  and and_7 (out_5[6], not_1_out, B, C, not_3_out);
  and and_8 (out_5[7], not_1_out, B, C, D);
  and and_9 (out_5[8], A, not_1_out, not_4_out, not_3_out);
  and and_10 (out_5[9], A, not_1_out, not_4_out, D);
  and and_11 (out_5[10], A, not_1_out, C, not_3_out);
  and and_12 (out_5[11], A, not_1_out, C, D);
  and and_13 (out_5[12], A, B, not_4_out, not_3_out);
  and and_14 (out_5[13], A, B, not_4_out, D);
  and and_15 (out_5[14], A, B, C, not_3_out);
  and and_16 (out_5[15], A, B, C, D);

  // Notes on the sheet:
  //   G0
  //   G1
  //   G2
  //   G3
  //   G4
  //   G5
  //   G6
  //   G7
  //   G8
  //   G9
  //   G10
  //   G11
  //   G12
  //   G13
  //   G14
  //   G15
endmodule
