// Logisim project ALU_Design.circ as structural Verilog: 4 circuits, main circuit main
module main (
  input  A,
  input  B,
  input  Cin,
  output S,
  output Cout
);

  wire nand_1_out, nand_2_out, nand_3_out, nand_4_out, nand_5_out, nand_6_out, nand_7_out, nand_8_out,
       nand_9_out, nand_10_out, nand_11_out, nand_12_out, nand_13_out, nand_14_out, nand_15_out, nand_16_out,
       nand_17_out, nand_18_out, nand_19_out, nand_20_out, nand_21_out, nand_22_out, nand_23_out,
       nand_25_out, nand_26_out, nand_27_out, nand_28_out;

  nand nand_1 (nand_1_out, A, A);
  nand nand_2 (nand_2_out, B, B);
  nand nand_3 (nand_3_out, A, A);
  nand nand_4 (nand_4_out, B, B);
  nand nand_5 (nand_5_out, B, Cin);
  nand nand_6 (nand_6_out, A, Cin);
  nand nand_7 (nand_7_out, nand_1_out, nand_2_out);
  nand nand_8 (nand_8_out, nand_3_out, B);
  nand nand_9 (nand_9_out, A, nand_4_out);
  nand nand_10 (nand_10_out, A, B);
  nand nand_11 (nand_11_out, nand_5_out, nand_6_out);
  nand nand_12 (nand_12_out, nand_7_out, nand_7_out);
  nand nand_13 (nand_13_out, nand_8_out, nand_8_out);
  nand nand_14 (nand_14_out, Cin, Cin);
  nand nand_15 (nand_15_out, nand_9_out, nand_9_out);
  nand nand_16 (nand_16_out, Cin, Cin);
  nand nand_17 (nand_17_out, nand_10_out, nand_10_out);
  nand nand_18 (nand_18_out, nand_11_out, nand_11_out);
  nand nand_19 (nand_19_out, A, B);
  nand nand_20 (nand_20_out, nand_12_out, Cin);
  nand nand_21 (nand_21_out, nand_13_out, nand_14_out);
  nand nand_22 (nand_22_out, nand_15_out, nand_16_out);
  nand nand_23 (nand_23_out, nand_17_out, Cin);
  nand nand_24 (Cout, nand_18_out, nand_19_out);
  nand nand_25 (nand_25_out, nand_20_out, nand_21_out);
  nand nand_26 (nand_26_out, nand_22_out, nand_23_out);
  nand nand_27 (nand_27_out, nand_25_out, nand_25_out);
  nand nand_28 (nand_28_out, nand_26_out, nand_26_out);
  nand nand_29 (S, nand_27_out, nand_28_out);
endmodule

module _8_bit_Adder (
  input  [3:0] A,
  input  [3:0] B,
  input  ADD_SUB,
  output [3:0] RES,
  output Cout,
  output Cin
);

  wire main_3_cout, main_4_cout;
  wire [3:0] multiplexer_1_out, not_1_out;

  main main_1 (.A(A[3]), .B(multiplexer_1_out[3]), .Cin(Cin), .S(RES[3]), .Cout(Cout));
  main main_2 (.A(A[2]), .B(multiplexer_1_out[2]), .Cin(main_3_cout), .S(RES[2]), .Cout(Cin));
  main main_3 (.A(A[1]), .B(multiplexer_1_out[1]), .Cin(main_4_cout), .S(RES[1]), .Cout(main_3_cout));
  main main_4 (.A(A[0]), .B(multiplexer_1_out[0]), .Cin(ADD_SUB), .S(RES[0]), .Cout(main_4_cout));
  Multiplexer #(.width(4), .enable("false")) multiplexer_1 (
    .in0(B), .in1(not_1_out), .out(multiplexer_1_out), .sel(ADD_SUB));
  assign not_1_out = ~B;  // NOT_Gate not_1, 4 bits wide
endmodule

module My_ALU (
  input  [3:0] A,
  input  [3:0] B,
  input  [2:0] Op_code,
  output [3:0] out_4
);

  wire [3:0] and_1_out, n8_bit_adder_1_res, or_1_out, xor_1_out;

  assign xor_1_out = A ^ B;  // XOR_Gate xor_1, 4 bits wide
  assign or_1_out = A | B;  // OR_Gate or_1, 4 bits wide
  assign and_1_out = A & B;  // AND_Gate and_1, 4 bits wide
  _8_bit_Adder u_8_bit_adder_1 (.A(A), .B(B), .ADD_SUB(Op_code[2]), .RES(n8_bit_adder_1_res));  // open: Cout, Cin
  Multiplexer #(.select(2), .width(4), .enable("false")) multiplexer_1 (
    .in0(xor_1_out), .in1(or_1_out), .in2(and_1_out), .in3(n8_bit_adder_1_res), .out(out_4),
    .sel(Op_code[1:0]));

  // Notes on the sheet:
  //   Op code 1
  //   Op code 2
endmodule

module My_ALU_Compare (
  input  [3:0] A,
  input  [3:0] B,
  input  [2:0] Op_code,
  output [3:0] out_4
);

  wire [3:0] and_1_out, n8_bit_adder_1_res, or_1_out, xor_1_out;

  assign xor_1_out = A ^ B;  // XOR_Gate xor_1, 4 bits wide
  assign or_1_out = A | B;  // OR_Gate or_1, 4 bits wide
  assign and_1_out = A & B;  // AND_Gate and_1, 4 bits wide
  _8_bit_Adder u_8_bit_adder_1 (.A(A), .B(B), .ADD_SUB(Op_code[2]), .RES(n8_bit_adder_1_res));  // open: Cout, Cin
  Multiplexer #(.select(2), .width(4), .enable("false")) multiplexer_1 (
    .in0(xor_1_out), .in1(or_1_out), .in2(and_1_out), .in3(n8_bit_adder_1_res), .out(out_4),
    .sel(Op_code[1:0]));

  // Notes on the sheet:
  //   Op code 1
  //   Op code 2
endmodule
