// Logisim project Register_with_enable.circ as structural Verilog: 4 circuits, main circuit Multiple_registers
module Multiple_registers (
  input  in_1,
  input  in_2,
  input  in_3,
  input  in_4,
  input  RD,
  input  WR,
  input  [7:0] in_7,
  output [7:0] out_8
);

  Register_with_enable register_with_enable_1 (
    .Register_Select(in_1), .Output(out_8), .nput(in_7), .s(WR), .e(RD));  // open: Memory
  Register_with_enable register_with_enable_2 (
    .Register_Select(in_2), .Output(out_8), .nput(in_7), .s(WR), .e(RD));  // open: Memory
  Register_with_enable register_with_enable_3 (
    .Register_Select(in_3), .Output(out_8), .nput(in_7), .s(WR), .e(RD));  // open: Memory
  Register_with_enable register_with_enable_4 (
    .Register_Select(in_4), .Output(out_8), .nput(in_7), .s(WR), .e(RD));  // open: Memory
endmodule

module Register_with_enable_test (
  input  in_1,
  input  in_2,
  input  in_3,
  input  [7:0] in_4,
  output [7:0] Register_Value,
  output [7:0] out_6
);

  Register_with_enable register_with_enable_1 (
    .Memory(Register_Value), .Register_Select(in_1), .Output(out_6), .nput(in_4), .s(in_3), .e(in_2));

  // Other names for the same wires on the sheet: R0_EN = in_1
endmodule

module Register_with_enable (
  input  [7:0] nput,
  input  Register_Select,
  input  s,
  input  e,
  output [7:0] Output,
  output [7:0] Memory
);

  wire and_1_out, and_2_out;
  wire [7:0] cpu_register_8_1_p5;

  and and_1 (and_1_out, Register_Select, s);
  and and_2 (and_2_out, Register_Select, e);
  assign Output = and_2_out ? cpu_register_8_1_p5 : 8'bz;  // Controlled_Buffer controlled_buffer_1
  // CPU_REGISTER_8 cpu_register_8_1: pin names not known; wires that end beside it: Memory, nput, and_1_out, and_2_out, cpu_register_8_1_p5

  // Notes on the sheet:
  //   nput: pull=down
  //   e: pull=down
  //   Register_Select: pull=down
  //   s: pull=down
  //   Output: pull=down
  //   Memory: pull=down
endmodule

module Registers_Decoders (
  input  in_1,
  input  [1:0] in_2,
  input  RD,
  input  WR,
  input  [7:0] in_5,
  output [7:0] out_6
);

  wire decoder_1_out0, decoder_1_out1, decoder_1_out2, decoder_1_out3;

  Decoder #(.select(2)) decoder_1 (
    .out0(decoder_1_out0), .out1(decoder_1_out1), .out2(decoder_1_out2), .out3(decoder_1_out3), .sel(in_2),
    .en(in_1));
  Register_with_enable register_with_enable_1 (
    .Register_Select(decoder_1_out0), .Output(out_6), .nput(in_5), .s(WR), .e(RD));  // open: Memory
  Register_with_enable register_with_enable_2 (
    .Register_Select(decoder_1_out1), .Output(out_6), .nput(in_5), .s(WR), .e(RD));  // open: Memory
  Register_with_enable register_with_enable_3 (
    .Register_Select(decoder_1_out2), .Output(out_6), .nput(in_5), .s(WR), .e(RD));  // open: Memory
  Register_with_enable register_with_enable_4 (
    .Register_Select(decoder_1_out3), .Output(out_6), .nput(in_5), .s(WR), .e(RD));  // open: Memory

  // Notes on the sheet:
  //   Input Data
  //   Output Data
endmodule
